# Fritzing sketch SR_Breadboard (saved by Fritzing 1.0.4)
breadboards: 1

parts:
  U1 = 74HC595 [package="DIP16 [THT]"]
  LED2 = LED - 3mm [color="Red (633nm)" current=0.030A package="3 mm [THT]"]
  WeMos_D1_Mini1 = WeMos D1 Mini  # not connected
  LED3 = LED - 3mm [color="Red (633nm)" current=0.030A package="3 mm [THT]"]
  LED4 = LED - 3mm [color="Red (633nm)" current=0.030A package="3 mm [THT]"]
  LED5 = LED - 3mm [color="Red (633nm)" current=0.030A package="3 mm [THT]"]
  LED6 = LED - 3mm [color="Red (633nm)" current=0.030A package="3 mm [THT]"]
  LED7 = LED - 3mm [color="Red (633nm)" current=0.030A package="3 mm [THT]"]
  LED8 = LED - 3mm [color="Red (633nm)" current=0.030A package="3 mm [THT]"]
  LED9 = LED - 3mm [color="Red (633nm)" current=0.030A package="3 mm [THT]"]
  R1 = Resistor [tolerance=±5% resistance=100 package="0805 [SMD]"]
  R2 = Resistor [tolerance=±5% resistance=100 package="0805 [SMD]"]
  R3 = Resistor [tolerance=±5% resistance=100 package="0805 [SMD]"]
  R4 = Resistor [tolerance=±5% resistance=100 package="0805 [SMD]"]
  R5 = Resistor [tolerance=±5% resistance=100 package="0805 [SMD]"]
  R6 = Resistor [tolerance=±5% resistance=100 package="0805 [SMD]"]
  R7 = Resistor [tolerance=±5% resistance=100 package="0805 [SMD]"]
  R8 = Resistor [tolerance=±5% resistance=100 package="0805 [SMD]"]

nets:
  N1: U1.Q1, LED3.anode
  N2: U1.Q2, LED4.anode
  N3: U1.Q3, LED5.anode
  N4: U1.Q4, LED6.anode
  N5: U1.Q5, LED7.anode
  N6: U1.Q6, LED8.anode
  N7: U1.Q7, LED9.anode
  N8: U1.GND, U1.MR, U1.OE, R1.Pin_1, R2.Pin_1, R3.Pin_1, R4.Pin_1, R5.Pin_1, R6.Pin_1, R7.Pin_1, R8.Pin_1
  N9: U1.Q0, LED2.anode
  N10: LED2.cathode, R8.Pin_0
  N11: LED3.cathode, R7.Pin_0
  N12: LED4.cathode, R6.Pin_0
  N13: LED5.cathode, R5.Pin_0
  N14: LED6.cathode, R4.Pin_0
  N15: LED7.cathode, R3.Pin_0
  N16: LED8.cathode, R2.Pin_0
  N17: LED9.cathode, R1.Pin_0
