# Fritzing sketch RGB_Array_Breadboard (saved by Fritzing 1.0.4)
breadboards: 1

parts:
  Part1 = NeoPixel NeoMatrix 8x8 [part_number=1487]
  WeMos_D1_Mini1 = WeMos D1 Mini

nets:
  VDD: Part1.VDD, WeMos_D1_Mini1.5V

custom parts:
  NeoPixel NeoMatrix 8x8: Put on your sunglasses before wiring up this LED matrix - 64 eye-blistering RGB LEDs adorn the NeoMatrix for a blast of configurable color. Arranged in an 8x8 matrix, each pixel is individually addressable. Only one microcontroller pin is required to control all the LEDs, and you get 24 bit color for each LED.
